// Digital circuit Debugger.dig as structural Verilog
module Debugger (
  input  [31:0] PC,
  input  Enable,
  input  Step,
  input  CLK,
  output D_CLK
);

  wire comparator_1_eq, multiplexer_1_out, or_1_out, register_1_q;
  wire [31:0] d_ff_1_q;

  D_FF #(.Bits(32)) d_ff_1 (.D(PC), .C(CLK), .Q(d_ff_1_q));  // open: nQ
  Comparator #(.Bits(32)) comparator_1 (.a(d_ff_1_q), .b(PC), .eq(comparator_1_eq));  // open: gt, lt
  or or_1 (or_1_out, ~comparator_1_eq, Step);  // Or
  Register register_1 (.D(comparator_1_eq), .C(CLK), .en(or_1_out), .Q(register_1_q));
  Multiplexer multiplexer_1 (.sel(register_1_q), .in_0(1'b0), .in_1(CLK), .out(multiplexer_1_out));
  Multiplexer multiplexer_2 (.sel(Enable), .in_0(CLK), .in_1(multiplexer_1_out), .out(D_CLK));
endmodule
