// Digital circuit Device2.dig as structural Verilog
module Device2 (
  input  CLK,
  input  [15:0] Addr,
  input  [5:0] Select,
  input  [31:0] Data_In,
  input  Write,
  output [31:0] Data
);

  wire and_1_out, comparator_1_eq;

  Comparator #(.Bits(6)) comparator_1 (.a(Select), .b(6'b000010), .eq(comparator_1_eq));  // open: gt, lt
  and and_1 (and_1_out, comparator_1_eq, Write);
  EEPROMDualPort #(.AddrBits(16), .Bits(32)) eepromdualport_1 (
    .A(Addr), .Din(Data_In), .str(and_1_out), .C(CLK), .ld(comparator_1_eq), .D(Data));

  // Notes on the sheet:
  //   MEMORY DEVICE 2
  //   contents of eepromdualport_1 (hex, n*v repeats v):
  //   1,5,1,4,1,2,1,2,5,5,5,9,1,4,1,5,1,4,1,2,1,2,5,5,5,4,9,1,5,1,4,1,4,1,2,1,2,5,5,5,3,
  //   9,1,1,1,4,1,4,1,2,1,2,5,5,5,3,9,1,3,1,5,1,4,1,2,1,2,5,5,5,3,9,1,5,1,4,1,4,1,2,1,2,
  //   5,5,5,3,9,1,2,1,2,1,2,1,4,5,5,5,9,1,5,1,4,1,4,1,2,1,2,5,5,5,3,9,1,2,1,5,1,4,1,2,1,
  //   2,5,5,5,4,9,1,4,1,5,1,4,1,2,1,2,5,5,5,3,9,1,5,1,4,1,4,1,2,1,2,5,5,5,3,9,1,2,1,5,1,
  //   4,1,2,1,2,5,5,5,3,9,1,2,1,2,1,2,1,4,5,5,5,9,1,9,1,5,1,4,1,2,1,2,5,5,5,3,9,1,1,1,5,
  //   1,4,1,2,1,2,5,5,5,4,9,1,5,1,5,1,4,1,2,1,2,5,5,5,3,9,1,2,1,5,1,4,1,2,1,2,5,5,5,3,9,
  //   1,2,1,2,1,2,1,4,5,5,5,9,1,2,1,5,1,4,1,2,1,2,5,5,5,4,9,1,1,1,4,1,4,1,2,1,2,5,5,5,3,
  //   9,1,3,1,5,1,4,1,2,1,2,5,5,5,4,9,1,5,1,4,1,4,1,2,1,2,5,5,5,3,9,1,6,1,4,1,4,1,2,1,2,
  //   5,5,5,4,9,1,2,1,2,1,2,1,4,5,5,5,9,8,1,0,1,0,c,1,0,1,0,c,9,1,3,1,0,c,1,1,3,1,3,1,0,
  //   d,1,3,1,3,1,0,c,d,1,a,4,1,3,1,5,1,2,5,5,1,4,3,1,5,1,2,5,5,1,5,3,f,1,8,1,4,1,4,1,4,
  //   5,5,3,9,1,5,1,4,1,4,1,4,5,5,3,9,1,4,1,5,1,4,1,4,5,5,4,9,1,4,1,5,1,4,1,4,5,5,4,9,1,
  //   1,1,5,1,4,1,4,5,5,4,9,1,2,1,4,1,4,5,5,9,1,1,1,3,1,0,c,4,1,3,1,0,d,1,3,1,3,1,0,c,c,
  //   1,3,1,0,c,1,4,1,5,1,2,5,5,1,7,3,1,5,1,2,5,5,1,1,3,f,1,0,1,1,c,1,3,1,0,d,2,9,1,1,1,
  //   3,1,0,c,4,1,0,1,0,c,1,3,1,0,d,1,5,1,5,1,2,5,5,1,2,3,1,5,1,2,5,5,1,9,3,f,1,1,1,2,1,
  //   4,1,4,5,5,3,9,1,a,9,1,9,1,4,1,4,1,4,5,5,3,9,1,2,1,4,1,4,5,5,9,1,1,1,4,1,4,1,4,5,5,
  //   3,9,1,3,1,5,1,4,1,4,5,5,4,9,1,2,1,4,1,4,5,5,9,1,1,1,4,1,4,1,4,5,5,3,9,1,2,1,4,1,4,
  //   5,5,9,1,3,1,4,1,4,1,4,5,5,3,9,1,1,1,5,1,4,1,4,5,5,4,9,1,3,1,5,1,4,1,4,5,5,4,9,1,5,
  //   1,4,1,4,5,5,9,1,5,1,5,1,4,1,4,5,5,3,9,1,4,1,5,1,4,1,4,5,5,3,9,1,5,1,4,1,4,1,4,5,5,
  //   3,9,1,2,1,5,1,4,1,4,5,5,3,9,1,2,1,4,1,4,5,5,9,1,4,1,5,1,4,1,4,5,5,3,9,1,8,1,4,1,4,
  //   1,4,5,5,3,9,1,1,1,4,1,4,1,4,5,5,3,9,1,4,1,5,1,4,1,4,5,5,3,9,1,2,1,4,1,4,5,5,9,1,2,
  //   1,5,1,4,1,4,5,5,3,9,1,5,1,5,1,4,1,4,5,5,3,9,1,2,1,5,1,4,1,4,5,5,4,9,1,3,1,5,1,4,1,
  //   4,5,5,3,9,1,2,1,4,1,4,5,5,9,1,1,1,5,1,4,1,4,5,5,4,9,1,2,1,5,1,4,1,4,5,5,4,9,1,2,1,
  //   4,1,4,5,5,9,1,3,1,4,1,4,1,4,5,5,3,9,1,8,1,4,1,4,1,4,5,5,3,9,1,9,1,4,1,4,1,4,5,5,3,
  //   9,1,3,1,4,1,4,1,4,5,5,3,9,1,5,1,5,1,4,1,4,5,5,4,9,1,5,1,4,1,4,1,4,5,5,3,9,1,2,1,5,
  //   1,4,1,4,5,5,4,9,1,1,1,2,1,4,1,4,5,5,3,9
endmodule
