// Digital circuit MemoryManagement.dig as structural Verilog
module MemoryManagement (
  input  [31:0] PC_In,
  input  [31:0] PD_In,
  input  [5:0] Dev,
  input  [15:0] Addr,
  input  Push,
  input  [31:0] Mem_In,
  input  Mem_Write,
  input  Pop,
  input  CLK,
  output PC_Write,
  output [31:0] PC_Out,
  output PD_Write,
  output [31:0] PD_Out,
  output [31:0] Mem_Out,
  output [31:0] Stack_Top
);

  wire Special_Purpose_p14, Special_Purpose_p15, Special_Purpose_p16;

  // Device0 Special_Purpose: pin names not known; wires that end beside it: CLK, Addr, Dev, Mem_In, Mem_Write, PC_In, PD_In, CLK, Addr, Dev, Mem_In, Mem_Write, Stack_Top, Special_Purpose_p14, Special_Purpose_p15, Special_Purpose_p16, Mem_Out, PC_Write, PD_Write
  // Device1 Stack: pin names not known; wires that end beside it: CLK, Addr, Dev, Mem_In, Mem_Write, Push, Pop, CLK, Addr, Dev, Mem_In, Mem_Write, Special_Purpose_p16, Special_Purpose_p15, Special_Purpose_p14, Stack_Top, Mem_Out
  // Device2 Kernel: pin names not known; wires that end beside it: CLK, Addr, Dev, Mem_In, Mem_Write, CLK, Addr, Dev, Mem_In, Mem_Write, Mem_Out
  // Device3 Kernel_RAM: pin names not known; wires that end beside it: CLK, Addr, Dev, Mem_In, Mem_Write, CLK, Addr, Dev, Mem_In, Mem_Write, Mem_Out
  // Device4 Screen: pin names not known; wires that end beside it: CLK, Addr, Dev, Mem_In, Mem_Write, CLK, Addr, Dev, Mem_In, Mem_Write, Mem_Out
  // Device5 device5_1: pin names not known; wires that end beside it: CLK, Addr, Dev, Mem_In, Mem_Write, CLK, Addr, Dev, Mem_In, Mem_Out, CLK, Addr, Dev, Mem_In

  assign PC_Out = Mem_Out;
  assign PD_Out = Mem_Out;
endmodule
