// Digital circuit main.dig as structural Verilog
module main (
  input  clk
);

  wire controlunit_1_p4, controlunit_1_p7, datapath_1_mem_write, datapath_1_pop, datapath_1_push;
  wire [2:0] controlunit_1_p12;
  wire [5:0] controlunit_1_p9;
  wire [15:0] add_1_s, controlunit_1_p8, MMU_stack_pointer;
  wire [27:0] controlunit_1_p11;
  wire [31:0] controlunit_1_p2, controlunit_1_p3, controlunit_1_p5, controlunit_1_p6, controlunit_1_p10,
       controlunit_1_p13, controlunit_1_p14, datapath_1_result, MMU_stack_top;

  // Probe PD on controlunit_1_p5
  // Probe PC on controlunit_1_p2
  // ControlUnit controlunit_1: pin names not known; wires that end beside it: clk, controlunit_1_p2, controlunit_1_p3, controlunit_1_p4, controlunit_1_p5, controlunit_1_p6, controlunit_1_p7, controlunit_1_p8, controlunit_1_p9, controlunit_1_p10, controlunit_1_p11, controlunit_1_p12, controlunit_1_p13, controlunit_1_p14
  // Probe ADDR on controlunit_1_p8
  // Probe DEV on controlunit_1_p9
  MemoryManagement MMU (
    .CLK(clk), .Addr(controlunit_1_p8), .Dev(controlunit_1_p9), .Mem_In(datapath_1_result),
    .Mem_Write(datapath_1_mem_write), .PC_In(controlunit_1_p2), .PD_In(controlunit_1_p5),
    .Push(datapath_1_push), .Pop(datapath_1_pop), .Mem_Out(controlunit_1_p10), .PC_Write(controlunit_1_p4),
    .PC_Out(controlunit_1_p3), .PD_Write(controlunit_1_p7), .PD_Out(controlunit_1_p6),
    .Stack_Top(MMU_stack_top), .Stack_Pointer(MMU_stack_pointer));
  // Probe INSTRUCTION on controlunit_1_p11
  Datapath datapath_1 (
    .CLK(clk), .Instr(controlunit_1_p11), .ConstIn(controlunit_1_p13), .NextLine(controlunit_1_p14),
    .MemIn(controlunit_1_p10), .StackTop(MMU_stack_top), .PZN(controlunit_1_p12), .Result(datapath_1_result),
    .Push(datapath_1_push), .Mem_Write(datapath_1_mem_write), .Pop(datapath_1_pop),
    .Mem_Addr(controlunit_1_p8), .Device_Select(controlunit_1_p9));
  // Probe MEM dec on controlunit_1_p10
  // Probe MEM hex on controlunit_1_p10
  // Probe MEM ascii on controlunit_1_p10
  // Probe STACK dec on MMU_stack_top
  // Probe STACK hex on MMU_stack_top
  // Probe STACK ascii on MMU_stack_top
  Add #(.Bits(16)) add_1 (.a(MMU_stack_pointer), .b(16'h1), .c_i(1'b0), .s(add_1_s));  // open: c_o
  // Probe Stack Size on add_1_s
  // Probe RESULT dec on datapath_1_result
  // Probe RESULT hex on datapath_1_result
  // Probe RESULT ascii on datapath_1_result
endmodule
