// Digital circuit Device0.dig as structural Verilog
module Device0 (
  input  [5:0] Select,
  input  [31:0] Addr,
  input  [31:0] Data_In,
  input  Write,
  input  [31:0] Stack_Top,
  input  [15:0] Stack_Pointer,
  input  CLK,
  input  [31:0] PC_In,
  input  [31:0] PD_In,
  output Data
);

  wire and_1_out, comparator_1_eq, comparator_2_gt;
  wire [15:0] add_1_s;
  wire [31:0] multiplexer_1_out, multiplexer_2_out, Subroutine_Stack_d;

  Comparator #(.Bits(6)) comparator_1 (.a(Select), .b({6{1'b0}}), .eq(comparator_1_eq));  // open: gt, lt
  Comparator comparator_2 (.a(Addr[0]), .b(1'b0), .gt(comparator_2_gt));  // open: eq, lt
  Add add_1 (.a(Addr[0]), .b(1'b0), .c_i(1'b0), .s(add_1_s[0]));  // open: c_o
  and and_1 (and_1_out, comparator_2_gt, comparator_1_eq);
  BlockRAMDualPort #(.AddrBits(16), .Bits(32)) Subroutine_Stack (
    .A(add_1_s), .Din(Data_In), .str(and_1_out), .C(CLK), .D(Subroutine_Stack_d));
  Multiplexer #(.Bits(32), .Selector_Bits(4)) multiplexer_1 (
    .in_0(Stack_Top), .in_1({{16{1'b0}}, Stack_Pointer}), .in_4(PC_In), .in_5(PD_In), .out(multiplexer_1_out));  // open: sel, in_2, in_3, in_6, in_7, in_8, in_9, in_10, in_11, in_12, in_13, in_14, in_15
  Multiplexer #(.Bits(32)) multiplexer_2 (
    .sel(and_1_out), .in_0(multiplexer_1_out), .in_1(Subroutine_Stack_d), .out(multiplexer_2_out));
  assign Data = comparator_1_eq ? multiplexer_2_out[0] : 1'bz;  // Driver driver_1
  // Pins of 1 and 32 bits meet at Addr
  // Pins of 1 and 16 bits meet at add_1_s
  // Pins of 1 and 16 bits meet at 16'ha
  // Pins of 1 and 32 bits meet at multiplexer_2_out

  // Notes on the sheet:
  //   MEMORY DEVICE 0
endmodule
